// Logisim project ex5.circ as structural Verilog: 5 circuits, main circuit rotr
module rotr (
  input  [15:0] A,
  input  [3:0] B,
  output [15:0] Out1
);

  wire [15:0] multiplexer_1_out, multiplexer_2_out, multiplexer_3_out, rot1_1_out_2, rot2_1_out_2,
       rot4_1_out_2, rot8_1_out_2;

  rot8 rot8_1 (.in_1(A), .out_2(rot8_1_out_2));
  Multiplexer #(.enable("false"), .width(16)) multiplexer_1 (
    .in0(A), .in1(rot8_1_out_2), .out(multiplexer_1_out), .sel(B[3]));
  rot4 rot4_1 (.in_1(multiplexer_1_out), .out_2(rot4_1_out_2));
  Multiplexer #(.enable("false"), .width(16)) multiplexer_2 (
    .in0(multiplexer_1_out), .in1(rot4_1_out_2), .out(multiplexer_2_out), .sel(B[2]));
  Multiplexer #(.enable("false"), .width(16)) multiplexer_3 (
    .in0(multiplexer_2_out), .in1(rot2_1_out_2), .out(multiplexer_3_out), .sel(B[1]));
  rot2 rot2_1 (.in_1(multiplexer_2_out), .out_2(rot2_1_out_2));
  rot1 rot1_1 (.in_1(multiplexer_3_out), .out_2(rot1_1_out_2));
  Multiplexer #(.enable("false"), .width(16)) multiplexer_4 (
    .in0(multiplexer_3_out), .in1(rot1_1_out_2), .out(Out1), .sel(B[0]));

  // Other names for the same wires on the sheet: A_t = B[0]; B_t = B[1]; C = B[2]; D = B[3]

  // Notes on the sheet:
  //   PUT CIRCUITRY HERE
endmodule

module rot8 (
  input  [15:0] in_1,
  output [15:0] out_2
);

  wire [15:0] rot4_1_out_2;

  rot4 rot4_1 (.in_1(in_1), .out_2(rot4_1_out_2));
  rot4 rot4_2 (.in_1(rot4_1_out_2), .out_2(out_2));

  // Notes on the sheet:
  //   PUT CIRCUITRY HERE
endmodule

module rot4 (
  input  [15:0] in_1,
  output [15:0] out_2
);

  wire [15:0] rot2_1_out_2;

  rot2 rot2_1 (.in_1(in_1), .out_2(rot2_1_out_2));
  rot2 rot2_2 (.in_1(rot2_1_out_2), .out_2(out_2));

  // Notes on the sheet:
  //   PUT CIRCUITRY HERE
endmodule

module rot2 (
  input  [15:0] in_1,
  output [15:0] out_2
);

  wire [15:0] rot1_1_out_2;

  rot1 rot1_1 (.in_1(in_1), .out_2(rot1_1_out_2));
  rot1 rot1_2 (.in_1(rot1_1_out_2), .out_2(out_2));

  // Notes on the sheet:
  //   PUT CIRCUITRY HERE
endmodule

module rot1 (
  input  [15:0] in_1,
  output [15:0] out_2
);


  assign out_2 = {in_1[0], in_1[15:1]};

  // Other names for the same wires on the sheet: B[14:0] = in_1[15:1]; A = in_1[0]

  // Notes on the sheet:
  //   PUT CIRCUITRY HERE
endmodule
